# Fritzing sketch esp32thing (saved by Fritzing 1.0.1rc)
circuit board: 9.6773cm x 7.17313cm

parts:
  Bauteil3 = GY-VL53L0XV2 Laser Ranger Module
  LevelShifter1 = I2C level shifter bidirectional
  LevelShifter2 = I2C level shifter bidirectional
  USB_to_Auger_Isolator(Main_Unit) = USB connector [package=THT]
  SparkFun_ESP32_Thing = SparkFun ESP32 Thing [part_number=DEV-13907]
  J2 = female pin header, 8 pins [form="♀ (female)"]
  J5 = female pin header, 8 pins [form="♀ (female)"]

nets:
  VCC: Bauteil3.VCC, LevelShifter1.LV, LevelShifter2.LV, SparkFun_ESP32_Thing.3.3V
  GND: Bauteil3.GND, LevelShifter1.GND, LevelShifter2.GND, SparkFun_ESP32_Thing.GND, J2.pin7
  N1: Bauteil3.SCL, SparkFun_ESP32_Thing.22
  N2: Bauteil3.SDA, SparkFun_ESP32_Thing.21
  N3: LevelShifter1.LV4, SparkFun_ESP32_Thing.16
  N4: LevelShifter1.LV3, SparkFun_ESP32_Thing.19
  N5: LevelShifter1.LV2, SparkFun_ESP32_Thing.U0RXD
  N6: LevelShifter1.LV1, SparkFun_ESP32_Thing.U0TXD
  N7: LevelShifter1.HV1, J2.pin4
  N8: LevelShifter1.HV2, J2.pin3
  N9: LevelShifter1.HV, LevelShifter2.HV, SparkFun_ESP32_Thing.VUSB-RAW, SparkFun_ESP32_Thing.V_BATT, J2.pin8
  N10: LevelShifter1.HV3, J2.pin6
  N11: LevelShifter1.HV4, J2.pin5
  N12: LevelShifter2.LV4, SparkFun_ESP32_Thing.25
  N13: LevelShifter2.LV3, SparkFun_ESP32_Thing.26
  N14: LevelShifter2.LV2, SparkFun_ESP32_Thing.27
  N15: LevelShifter2.LV1, SparkFun_ESP32_Thing.14
  N16: LevelShifter2.HV1, J5.pin5
  N17: LevelShifter2.HV2, USB_to_Auger_Isolator(Main_Unit).5V
  N18: LevelShifter2.HV3, J5.pin8
  N19: LevelShifter2.HV4, USB_to_Auger_Isolator(Main_Unit).d+

notes:
  GPIO25 --> LS --> Auger Isolater (output)
  GPIO26 --> LS --> Reset (output)
  GPIO27 --> LS --> Auger Isolator (input)
  GPIO14 --> LS --> Timer LED (output) (changed from GPIO19 due to layout)
  GPIO19(RX1) --> LS --> RX Display Board
  (changed from GPIO21 due to ToF(SDA))
  GPIO01(TX0) --> LS --> TuyaMCU(RX)
  GPIO03(RX0) --> LS --> TuyaMCU(TX)
  GPIO16(RX2) --> LS --> TX Display Board
  GPIO32 --> NLS --> SDA
  GPIO33 --> NLS --> SCL
  GPIO25 --> NLS --> Auger Isolater (output)
  GPIO26 --> NLS --> Auger Isolator (input)
  GPIO21(RX1) --> LS --> TX Display Board
  GPIO01(TX0) --> LS --> TuyaMCU(RX)
  GPIO03(RX0) --> LS --> TuyaMCU(TX)
  GPIO22(RX2) --> LS --> RX Display Board
  GPIO19 --> LS --> Timer LED (output)
  GPIO23 --> LS --> Reset (output)

custom parts:
  GY-VL53L0XV2 Laser Ranger Module: The GY-VL53L0XV2 is based on the VL53L0X from ST Microelectronics, a time-of-flight ranging system integrated into a compact module.
  SparkFun ESP32 Thing: The SparkFun ESP32 Thing is a comprehensive development platform for Espressif’s ESP32, their super-charged version of the popular ESP8266. Like the 8266, the ESP32 is a WiFi-compatible microcontroller, but to that it adds support for Bluetooth low-energy (i.e BLE, BT4.0, Bluetooth Smart), and nearly 30 I/O pins. The ESP32’s power and versatility will make it the foundation of IoT and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
