# Fritzing sketch esp32thing_v3 (saved by Fritzing 1.0.1rc)
circuit board: 9.6773cm x 7.17313cm

parts:
  Bauteil3 = GY-VL53L0XV2 Laser Ranger Module
  USB_to_Auger_Isolator(Main_Unit) = USB connector [package=THT]
  SparkFun_ESP32_Thing = SparkFun ESP32 Thing [part_number=DEV-13907]
  J2 = female pin header, 8 pins [form="♀ (female)"]
  J5 = female pin header, 8 pins [form="♀ (female)"]
  Bauteil4 = TXB0108 8-channel Bi-directional Logic Level Converter
  Bauteil5 = TXB0108 8-channel Bi-directional Logic Level Converter

nets:
  VCC: Bauteil3.VCC, SparkFun_ESP32_Thing.3.3V, Bauteil4.OE, Bauteil4.VCCA, Bauteil5.VCCA
  GND: Bauteil3.GND, SparkFun_ESP32_Thing.GND, J2.pin7, Bauteil4.GND
  N1: Bauteil3.SCL, SparkFun_ESP32_Thing.21
  N2: Bauteil3.SDA, SparkFun_ESP32_Thing.22
  N3: USB_to_Auger_Isolator(Main_Unit).5V, Bauteil5.B2
  N4: USB_to_Auger_Isolator(Main_Unit).d+, Bauteil5.B4
  N5: SparkFun_ESP32_Thing.VUSB-RAW, SparkFun_ESP32_Thing.V_BATT, J2.pin8, Bauteil4.VCCB, Bauteil5.VCCB
  N6: SparkFun_ESP32_Thing.27, Bauteil5.A2
  N7: SparkFun_ESP32_Thing.26, Bauteil5.A3
  N8: SparkFun_ESP32_Thing.25, Bauteil5.A4
  N9: SparkFun_ESP32_Thing.35, Bauteil5.A5
  N10: SparkFun_ESP32_Thing.16, Bauteil4.A4
  N11: SparkFun_ESP32_Thing.17, Bauteil4.A1
  N12: SparkFun_ESP32_Thing.19, Bauteil4.A5
  N13: SparkFun_ESP32_Thing.U0RXD, Bauteil4.A3
  N14: SparkFun_ESP32_Thing.U0TXD, Bauteil4.A2
  N15: J2.pin3, Bauteil4.B3
  N16: J2.pin4, Bauteil4.B2
  N17: J2.pin5, Bauteil4.B1
  N18: J2.pin6, Bauteil4.B4
  N19: J5.pin4, J5.pin5, Bauteil4.B5
  N20: J5.pin7, J5.pin8, Bauteil5.B3

notes:
  GPIO21 --> NLS --> SDA
  GPIO22 --> NLS --> SCL
  GPIO25 --> LS --> Auger Isolater (Output)
  GPIO27 --> LS --> Auger Isolator (Input)
  GPIO35 --> LS --> Power LED(Input, LOW)
  GPIO19 --> LS --> Timer LED (output)
  GPIO16 --> LS --> TX Display Board
  GPIO01(TX) --> LS --> TuyaMCU(RX)
  GPIO03(RX) --> LS --> TuyaMCU(TX)
  GPIO17 --> LS --> RX Display Board
  GPIO19 --> LS --> Timer LED (output)
  GPIO26 --> LS --> Thumbs Up Button

custom parts:
  GY-VL53L0XV2 Laser Ranger Module: The GY-VL53L0XV2 is based on the VL53L0X from ST Microelectronics, a time-of-flight ranging system integrated into a compact module.
  SparkFun ESP32 Thing: The SparkFun ESP32 Thing is a comprehensive development platform for Espressif’s ESP32, their super-charged version of the popular ESP8266. Like the 8266, the ESP32 is a WiFi-compatible microcontroller, but to that it adds support for Bluetooth low-energy (i.e BLE, BT4.0, Bluetooth Smart), and nearly 30 I/O pins. The ESP32’s power and versatility will make it the foundation of IoT and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
  TXB0108 8-channel Bi-directional Logic Level Converter: Because the Arduino (and Basic Stamp) are 5V devices, and most modern sensors, displays, flash cards and modes are 3.3V-only, many makers find that they need to perform level shifting/conversion to protect the 3.3V device from 5V. Although one can use resistors to make a divider, for high speed transfers, the resistors can add a lot of slew and cause havoc that is tough to debug. For that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
